# Fritzing sketch Moduls_and_connection_between_modules (saved by Fritzing 0.9.3b)
breadboards: 1
stripboards: 1

parts:
  Part1 = Arduino Nano (Rev3.0) (ICSP)
  Raspberry_Pi_Zero1 = Raspberry Pi Zero
  R1 = Resistor [tolerance=±5% resistance=4.7k package=THT]

nets:
  N1: Part1.D1/TX, Raspberry_Pi_Zero1.GPIO15
  N2: Part1.D0/RX, Raspberry_Pi_Zero1.GPIO14
  GND: Part1.GND, Raspberry_Pi_Zero1.GND
  5V: Part1.5V, Raspberry_Pi_Zero1.5V, R1.Pin_1
  N3: Raspberry_Pi_Zero1.GPIO4, R1.Pin_0
